// Logisim project circ.circ as structural Verilog: 2 circuits, main circuit main
module main (
  input  vTh,
  input  I_n,
  input  _140,
  input  c,
  input  d
);

  wire comparator_1_eq, register_30_q;
  wire [7:0] adder_1_out, adder_2_out, adder_3_out, adder_4_out, adder_5_out, adder_6_out, adder_7_out,
       adder_8_out, multiplexer_1_out, multiplexer_2_out, multiplier_1_out, negator_1_out, register_1_q,
       register_2_q, register_3_q, register_4_q, register_5_q, register_6_q, register_7_q, register_8_q,
       register_9_q, register_10_q, register_11_q, register_12_q, register_13_q, register_14_q,
       register_15_q, register_16_q, register_17_q, register_18_q, register_19_q, register_20_q,
       register_21_q, register_22_q, register_23_q, register_24_q, register_25_q, register_26_q,
       register_27_q, register_28_q, register_29_q, register_31_q, register_32_q, register_33_q,
       register_34_q, shifter_1_out, shifter_2_out, shifter_3_out, shifter_4_out, shifter_5_out, undriven,
       undriven_2, undriven_3, undriven_4, undriven_5;

  Register register_1 (.Q(register_1_q));  // open: D, en, clk, clr
  Register register_2 (.Q(register_2_q));  // open: D, en, clk, clr
  Multiplier multiplier_1 (.a(register_1_q), .b(register_1_q), .out(multiplier_1_out));  // open: cin, cout
  Shifter #(.shift("lr")) shifter_1 (.in(register_1_q), .out(shifter_1_out));  // open: dist
  Negator negator_1 (.in(register_2_q), .out(negator_1_out));
  Register register_3 (.D(register_1_q), .Q(register_3_q));  // open: en, clk, clr
  Register register_4 (.D(multiplier_1_out), .Q(register_4_q));  // open: en, clk, clr
  Register register_5 (.D(register_1_q), .Q(register_5_q));  // open: en, clk, clr
  Register register_6 (.D(shifter_1_out), .Q(register_6_q));  // open: en, clk, clr
  Register register_7 (.D(negator_1_out), .Q(register_7_q));  // open: en, clk, clr
  Register register_8 (.D(register_2_q), .Q(register_8_q));  // open: en, clk, clr
  Shifter #(.shift("lr")) shifter_2 (.in(register_4_q), .out(shifter_2_out));  // open: dist
  Shifter shifter_3 (.in(register_5_q), .out(shifter_3_out));  // open: dist
  Adder adder_1 (.a(register_6_q), .b(register_7_q), .out(adder_1_out));  // open: cin, cout
  Register register_9 (.D(register_3_q), .Q(register_9_q));  // open: en, clk, clr
  Register register_10 (.D(shifter_2_out), .Q(register_10_q));  // open: en, clk, clr
  Register register_11 (.D(shifter_3_out), .Q(register_11_q));  // open: en, clk, clr
  Register register_12 (.D(undriven), .Q(register_12_q));  // open: en, clk, clr
  Register register_13 (.D(undriven_2), .Q(register_13_q));  // open: en, clk, clr
  Register register_14 (.D(adder_1_out), .Q(register_14_q));  // open: en, clk, clr
  Register register_15 (.D(register_7_q), .Q(register_15_q));  // open: en, clk, clr
  Register register_16 (.D(register_8_q), .Q(register_16_q));  // open: en, clk, clr
  Adder adder_2 (.a(register_10_q), .b(register_11_q), .out(adder_2_out));  // open: cin, cout
  Adder adder_3 (.a(register_12_q), .b(register_13_q), .out(adder_3_out));  // open: cin, cout
  Adder adder_4 (.a(adder_3_out), .b(register_15_q), .out(adder_4_out));  // open: cin, cout
  Shifter shifter_4 (.in(register_14_q), .out(shifter_4_out));  // open: dist
  Register register_17 (.D(register_9_q), .Q(register_17_q));  // open: en, clk, clr
  Register register_18 (.D(adder_5_out), .Q(register_18_q));  // open: en, clk, clr
  Adder adder_5 (.a(adder_2_out), .b(adder_4_out), .out(adder_5_out));  // open: cin, cout
  Register register_19 (.D(shifter_4_out), .Q(register_19_q));  // open: en, clk, clr
  Register register_20 (.D(register_16_q), .Q(register_20_q));  // open: en, clk, clr
  Shifter shifter_5 (.in(register_18_q), .out(shifter_5_out));  // open: dist
  Adder adder_6 (.a(register_19_q), .b(register_20_q), .out(adder_6_out));  // open: cin, cout
  Register register_21 (.D(register_17_q), .Q(register_21_q));  // open: en, clk, clr
  Register register_22 (.D(shifter_5_out), .Q(register_22_q));  // open: en, clk, clr
  Register register_23 (.D(adder_6_out), .Q(register_23_q));  // open: en, clk, clr
  Register register_24 (.D(undriven_3), .Q(register_24_q));  // open: en, clk, clr
  Adder adder_7 (.a(register_21_q), .b(register_22_q), .out(adder_7_out));  // open: cin, cout
  Adder adder_8 (.a(register_23_q), .b(register_24_q), .out(adder_8_out));  // open: cin, cout
  Register register_25 (.D(undriven_4), .Q(register_25_q));  // open: en, clk, clr
  Register register_26 (.D(adder_7_out), .Q(register_26_q));  // open: en, clk, clr
  Register register_27 (.D(undriven_5), .Q(register_27_q));  // open: en, clk, clr
  Register register_28 (.D(register_23_q), .Q(register_28_q));  // open: en, clk, clr
  Register register_29 (.D(adder_8_out), .Q(register_29_q));  // open: en, clk, clr
  Comparator comparator_1 (.a(register_25_q), .b(register_26_q), .eq(comparator_1_eq));  // open: gt, lt
  Register #(.width(1)) register_30 (.D(comparator_1_eq), .Q(register_30_q));  // open: en, clk, clr
  Register register_31 (.D(register_26_q), .Q(register_31_q));  // open: en, clk, clr
  Register register_32 (.D(register_27_q), .Q(register_32_q));  // open: en, clk, clr
  Register register_33 (.D(register_28_q), .Q(register_33_q));  // open: en, clk, clr
  Register register_34 (.D(register_29_q), .Q(register_34_q));  // open: en, clk, clr
  Multiplexer #(.width(8), .enable("false")) multiplexer_1 (
    .in0(register_31_q), .in1(register_32_q), .out(multiplexer_1_out), .sel(register_30_q));
  Multiplexer #(.width(8), .enable("false")) multiplexer_2 (
    .in0(register_33_q), .in1(register_34_q), .out(multiplexer_2_out), .sel(register_30_q));
  Register register_35 (.D(multiplexer_1_out));  // open: en, Q, clk, clr
  Register register_36 (.D(multiplexer_2_out));  // open: en, Q, clk, clr

  // Notes on the sheet:
  //   1
  //   v_n
  //   u_n
  //   v_n^2
  //   b * v_n
  //   2
  //   0.04 * v_n^2
  //   5* v_n
  //   3
  //   du_n/(a * dt)  -->  du_n
  //   4
  //   dv_n/dt  -->  dv_n
  //   du_n + u_n
  //   5
  //   dv_n + v_n
  //   6
  //   7
  //   v_n + 1
  //   u_n + 1
endmodule

module calcQuadrado (
  input  [1:0] in_1,
  output [1:0] out_2,
  output [1:0] out_3
);

  Multiplier #(.width(2)) multiplier_1 (.a(in_1), .b(in_1), .out(out_2), .cout(out_3));  // open: cin
endmodule
