// Logisim project circ_original.circ as structural Verilog: 2 circuits, main circuit main
module main (
  input  vTh,
  input  I_n,
  input  _140,
  input  c,
  input  d
);

  wire comparator_1_eq;
  wire [7:0] adder_1_out, adder_2_out, adder_3_out, adder_4_out, adder_5_out, adder_6_out, adder_7_out,
       adder_8_out, multiplexer_1_out, multiplexer_2_out, multiplier_1_out, negator_1_out, register_1_q,
       register_2_q, register_3_q, register_4_q, register_5_q, register_6_q, register_7_q, register_8_q,
       register_9_q, register_10_q, register_11_q, register_12_q, register_13_q, register_14_q,
       register_15_q, register_16_q, register_17_q, register_18_q, shifter_1_out, shifter_2_out,
       shifter_3_out, shifter_4_out, shifter_5_out, undriven, undriven_2, undriven_3, undriven_4, undriven_5;

  Register register_1 (.D(multiplexer_1_out), .Q(register_1_q));  // open: en, clk, clr
  Register register_2 (.D(multiplexer_2_out), .Q(register_2_q));  // open: en, clk, clr
  Multiplier multiplier_1 (.a(register_1_q), .b(register_1_q), .out(multiplier_1_out));  // open: cin, cout
  Shifter #(.shift("lr")) shifter_1 (.in(register_1_q), .out(shifter_1_out));  // open: dist
  Negator negator_1 (.in(register_2_q), .out(negator_1_out));
  Register register_3 (.D(multiplier_1_out), .Q(register_3_q));  // open: en, clk, clr
  Register register_4 (.D(shifter_1_out), .Q(register_4_q));  // open: en, clk, clr
  Register register_5 (.D(negator_1_out), .Q(register_5_q));  // open: en, clk, clr
  Shifter #(.shift("lr")) shifter_2 (.in(register_3_q), .out(shifter_2_out));  // open: dist
  Shifter shifter_3 (.in(register_1_q), .out(shifter_3_out));  // open: dist
  Adder adder_1 (.a(register_4_q), .b(register_5_q), .out(adder_1_out));  // open: cin, cout
  Register register_6 (.D(shifter_2_out), .Q(register_6_q));  // open: en, clk, clr
  Register register_7 (.D(shifter_3_out), .Q(register_7_q));  // open: en, clk, clr
  Register register_8 (.D(undriven), .Q(register_8_q));  // open: en, clk, clr
  Register register_9 (.D(undriven_2), .Q(register_9_q));  // open: en, clk, clr
  Register register_10 (.D(adder_1_out), .Q(register_10_q));  // open: en, clk, clr
  Adder adder_2 (.a(register_6_q), .b(register_7_q), .out(adder_2_out));  // open: cin, cout
  Adder adder_3 (.a(register_8_q), .b(register_9_q), .out(adder_3_out));  // open: cin, cout
  Adder adder_4 (.a(adder_3_out), .b(register_5_q), .out(adder_4_out));  // open: cin, cout
  Shifter shifter_4 (.in(register_10_q), .out(shifter_4_out));  // open: dist
  Adder adder_5 (.a(adder_2_out), .b(adder_4_out), .out(adder_5_out));  // open: cin, cout
  Register register_11 (.D(adder_5_out), .Q(register_11_q));  // open: en, clk, clr
  Register register_12 (.D(shifter_4_out), .Q(register_12_q));  // open: en, clk, clr
  Shifter shifter_5 (.in(register_11_q), .out(shifter_5_out));  // open: dist
  Adder adder_6 (.a(register_12_q), .b(register_2_q), .out(adder_6_out));  // open: cin, cout
  Register register_13 (.D(shifter_5_out), .Q(register_13_q));  // open: en, clk, clr
  Register register_14 (.D(adder_6_out), .Q(register_14_q));  // open: en, clk, clr
  Register register_15 (.D(undriven_3), .Q(register_15_q));  // open: en, clk, clr
  Adder adder_7 (.a(register_1_q), .b(register_13_q), .out(adder_7_out));  // open: cin, cout
  Adder adder_8 (.a(register_14_q), .b(register_15_q), .out(adder_8_out));  // open: cin, cout
  Register register_16 (.D(undriven_4), .Q(register_16_q));  // open: en, clk, clr
  Register register_17 (.D(adder_7_out), .Q(register_17_q));  // open: en, clk, clr
  Register register_18 (.D(undriven_5), .Q(register_18_q));  // open: en, clk, clr
  Comparator comparator_1 (.a(register_16_q), .b(register_17_q), .eq(comparator_1_eq));  // open: gt, lt
  Multiplexer #(.width(8), .enable("false")) multiplexer_1 (
    .in0(register_17_q), .in1(register_18_q), .out(multiplexer_1_out), .sel(comparator_1_eq));
  Multiplexer #(.width(8), .enable("false")) multiplexer_2 (
    .in0(register_14_q), .in1(adder_8_out), .out(multiplexer_2_out), .sel(comparator_1_eq));

  // Notes on the sheet:
  //   ciclo 1
  //   v_n
  //   u_n
  //   v_n^2
  //   b * v_n
  //   ciclo 2
  //   1
  //   2
  //   3
  //   0.04 * v_n^2
  //   5* v_n
  //   ciclo 3
  //   4
  //   5
  //   6
  //   7
  //   8
  //   du_n/(a * dt)  -->  du_n
  //   ciclo 4
  //   9
  //   10
  //   dv_n/dt  -->  dv_n
  //   du_n + u_n
  //   12
  //   ciclo 5
  //   11
  //   13
  //   dv_n + v_n
  //   ciclo 6
  //   14
  //   15
  //   16
  //   v_n + 1
  //   u_n + 1
endmodule

module calcQuadrado (
  input  [1:0] in_1,
  output [1:0] out_2,
  output [1:0] out_3
);

  Multiplier #(.width(2)) multiplier_1 (.a(in_1), .b(in_1), .out(out_2), .cout(out_3));  // open: cin
endmodule
